# Fritzing sketch fritzing (saved by Fritzing 0.9.3b)

parts:
  Componente1 = Arduino Uno (Rev3)
  U2 = RELAY [package=relay-jzc]

nets:
  N1: Componente1.D12/MISO, U2.COIL2
  N2: Componente1.5V, U2.NO
